# Fritzing sketch ds3231-with-ssd1306-wiring (saved by Fritzing 0.9.4)
breadboards: 1

parts:
  ZS-042_RTC1 = ZS-042 RTC Module
  Part1 = Arduino Nano (Rev3.0) (ICSP)
  S1 = Pushbutton [package="[THT]"]
  R1 = Resistor [tolerance=±5% resistance=220 package=THT]
  D1 = P1000K [part_number=P1000K]
  YwRobot_Power_Supply1 = YwRobot Breadboard Power Supply [part_number=545043]
  OLED1 = OLED 128x64 I2C Monochrome Display

nets:
  GND: ZS-042_RTC1.GND, YwRobot_Power_Supply1.GND#11, YwRobot_Power_Supply1.GND#12, OLED1.GND
  VCC: ZS-042_RTC1.VCC, YwRobot_Power_Supply1.VCC#5, YwRobot_Power_Supply1.VCC#6, OLED1.VDD
  N1: ZS-042_RTC1.SDA, Part1.A4
  N2: ZS-042_RTC1.SCL, Part1.A5
  N3: ZS-042_RTC1.SQW, Part1.D2
  N4: Part1.GND, D1.anode
  N5: Part1.D4, S1.Pin_3, S1.Pin_4, R1.Pin_1
  N6: S1.Pin_1, S1.Pin_2
  N7: R1.Pin_0, D1.cathode
  N8: YwRobot_Power_Supply1.VCC#9, YwRobot_Power_Supply1.VCC#10
  N9: YwRobot_Power_Supply1.GND#13, YwRobot_Power_Supply1.GND#14

notes:
  1K ohm
  3.3V

custom parts:
  YwRobot Breadboard Power Supply: The YwRobot Breadboard Power Supply (MB-V2) has two power rails; they can be 5V or 3V3. Power to the module can be provided through the female USB socket or through the A10 (female) 2.1mm power jack.
