# Fritzing sketch ds3231-with-unl2003-serial-wiring (saved by Fritzing 0.9.4)
breadboards: 1

parts:
  ZS-042_RTC1 = ZS-042 RTC Module
  Part1 = Arduino Nano (Rev3.0) (ICSP)
  S1 = Pushbutton [package="[THT]"]
  R1 = Resistor [tolerance=±5% resistance=220 package=THT]
  D1 = P1000K [part_number=P1000K]
  YwRobot_Power_Supply1 = YwRobot Breadboard Power Supply [part_number=545043]
  UNL2003A_Breakout_Board = ULN2003A breakout board
  MOTOR1 = 28BYJ-48 Stepper Motor  # not connected

nets:
  N1: ZS-042_RTC1.GND, YwRobot_Power_Supply1.GND#11, YwRobot_Power_Supply1.GND#12, UNL2003A_Breakout_Board.0V
  VCC: ZS-042_RTC1.VCC, YwRobot_Power_Supply1.VCC#5, YwRobot_Power_Supply1.VCC#6, UNL2003A_Breakout_Board.+5V
  N2: ZS-042_RTC1.SDA, Part1.A4
  N3: ZS-042_RTC1.SCL, Part1.A5
  N4: ZS-042_RTC1.SQW, Part1.D2
  N5: Part1.GND, D1.anode
  N6: Part1.D4, S1.Pin_3, S1.Pin_4, R1.Pin_1
  N7: Part1.D8, UNL2003A_Breakout_Board.In_1
  N8: Part1.D9, UNL2003A_Breakout_Board.In_2
  N9: Part1.D10, UNL2003A_Breakout_Board.In_3
  N10: Part1.D11/MOSI, UNL2003A_Breakout_Board.In_4
  N11: S1.Pin_1, S1.Pin_2
  N12: R1.Pin_0, D1.cathode
  N13: YwRobot_Power_Supply1.VCC#9, YwRobot_Power_Supply1.VCC#10
  N14: YwRobot_Power_Supply1.GND#13, YwRobot_Power_Supply1.GND#14

notes:
  1K ohm
  5V out
  28BYJ-48
  5V in
  9V in

custom parts:
  YwRobot Breadboard Power Supply: The YwRobot Breadboard Power Supply (MB-V2) has two power rails; they can be 5V or 3V3. Power to the module can be provided through the female USB socket or through the A10 (female) 2.1mm power jack.
  ULN2003A breakout board: ULN2003A 7-way Darlington Transistor Driver on breakoutboard
